# Fritzing sketch arduino-schematic (saved by Fritzing 0.9.3b)
breadboards: 1

parts:
  R2 = Resistor [tolerance=±5% resistance=300 package=THT]
  LED1 = LED - 5mm [color="Red (633nm)" package="5 mm [THT]"]
  J1 = Piezo Speaker
  S2 = SWITCH-MOMENTARY-2 [package=reed_switch_pth]
  VCC1 = 4 x AAA Battery Mount
  U1 = atmega328 [package=dip]
  XTAL1 = Crystal [frequency="16 Mhz" package=THT]
  C1 = Ceramic Capacitor [capacitance=22nF package="100 mil [THT, multilayer]"]
  C2 = Ceramic Capacitor [capacitance=22nF package="100 mil [THT, multilayer]"]
  R3 = Resistor [tolerance=±5% resistance=10k package=THT]

nets:
  N1: R2.Pin_0, U1.D11_(PWM)
  N2: R2.Pin_1, LED1.anode
  GND: LED1.cathode, J1.pin1, VCC1.+, U1.GND, C1.0, C2.0
  N3: J1.pin2, U1.A2
  N4: S2.1, U1.VCC, R3.Pin_0
  N5: S2.2, VCC1.-
  N6: U1.RESET, R3.Pin_1
  N7: U1.XLAT1, XTAL1.pin_1, C1.1
  N8: U1.XLAT2, XTAL1.pin_0, C2.1
